// Logisim project 4_bit_ripple_adder.circ as structural Verilog: 1 circuit, main circuit main
module main (
);

  wire and_1_out, and_2_out, and_3_out, and_4_out, and_5_out, and_6_out, and_7_out, or_1_out, or_2_out,
       or_3_out, xor_1_out, xor_2_out, xor_3_out, xor_4_out, xor_5_out, xor_6_out, xor_7_out;

  xor xor_1 (xor_1_out, 1'b1, 1'b0);
  xor xor_2 (xor_2_out, 1'b1, 1'b0);
  xor xor_3 (xor_3_out, 1'b1, 1'b0);
  xor xor_4 (xor_4_out, 1'b0, 1'b1);
  LED led_1 (.in(xor_4_out));
  and and_1 (and_1_out, 1'b1, 1'b0);
  and and_2 (and_2_out, 1'b1, 1'b0);
  and and_3 (and_3_out, 1'b1, 1'b0);
  and and_4 (and_4_out, 1'b1, 1'b0);
  xor xor_5 (xor_5_out, xor_1_out, and_1_out);
  and and_5 (and_5_out, xor_1_out, and_1_out);
  xor xor_6 (xor_6_out, xor_2_out, or_1_out);
  and and_6 (and_6_out, xor_2_out, or_1_out);
  and and_7 (and_7_out, xor_3_out, or_2_out);
  LED led_2 (.in(xor_5_out));
  or or_1 (or_1_out, and_5_out, and_2_out);
  LED led_3 (.in(xor_6_out));
  or or_2 (or_2_out, and_6_out, and_3_out);
  xor xor_7 (xor_7_out, xor_3_out, or_2_out);
  LED led_4 (.in(xor_7_out));
  LED led_5 (.in(or_3_out));
  or or_3 (or_3_out, and_7_out, and_4_out);
endmodule
